# Fritzing sketch WiringDiagram (saved by Fritzing 0.9.3b)
breadboards: 1

parts:
  U1 = LCD-16X2 [package=lcd-16x2_noholes]
  Part1 = Arduino Uno (Rev3) - ICSP
  S1 = SWITCH-MOMENTARY-2 [package=tactile-pth]
  R1 = Resistor [tolerance=±5% resistance=10k package=THT]
  R2 = Temperature Sensor (Thermistor) [thermistor_type=NTC package=THT]
  R3 = Resistor [tolerance=±5% resistance=10k package=THT]
  R4 = Trimmer Potentiometer [maximum_resistance=10kΩ package=THT]

nets:
  VSS: U1.VSS, U1.K, Part1.GND, R1.Pin_0, R3.Pin_1, R4.leg2
  VDD: U1.VDD, U1.A, Part1.5V, S1.2, R2.pin_0, R4.leg1
  N1: U1.VO, R4.wiper
  N2: U1.RS, Part1.D7
  N3: U1.E, Part1.D8
  N4: U1.DB4, Part1.D9_PWM
  N5: U1.DB5, Part1.D10_PWM/SS
  N6: U1.DB6, Part1.D11_PWM/MOSI
  N7: U1.DB7, Part1.D12/MISO
  N8: Part1.A0, R3.Pin_0
  N9: Part1.D2, S1.1
